# Fritzing sketch grzalka_wiatrak_przekaznik_tranzystor (saved by Fritzing 0.9.3b)
breadboards: 2

parts:
  Part1 = Arduino Nano (Rev3.0)
  R1 = Resistor [tolerance=±5% resistance=220 package=THT]
  Part2 = Variable Capacitor [capacitance=100nF max_capacitance=10pF min_capacitance=2pF voltage=35V]
  A1 = 1 chan 3v relay module
  R2 = Temperature Sensor (Thermistor) [thermistor_type=NTC package=THT]
  Q1 = Basic FET N-Channel [package="D2Pak [SMD]"]
  R3 = Resistor [tolerance=±5% resistance=220 package=THT]  # not connected
  J1 = Peltier Element
  J2 = ATX24 Pin Power Supply Connector [package=atx24_right_angle]
  Part3 = LilyPad Buzzer  # not connected

nets:
  N1: Part1.GND, R1.Pin_1, Part2.1, Q1.source
  N2: Part1.D9, A1.pin_2
  N3: Part1.5V, A1.pin_1, R2.pin_1
  N4: Part1.A1, R1.Pin_0, Part2.0, R2.pin_0
  N5: A1.pin_7, J2.-12V
  N6: Q1.drain, J1.pin2
  N7: J1.pin1, J2.3.3V

custom parts:
  1 chan 3v relay module: Single 3V relay isolated drive control module High level drive board.
